# Fritzing sketch TemperatureSpeakerKom (saved by Fritzing 0.9.3b)
circuit board: 13.5398cm x 9.15531cm
breadboards: 2

parts:
  512 = 24LC512 [chip_label=512 package="DIP (Dual Inline) [THT]"]
  R1 = Resistor [tolerance=±5% resistance=2.2k package=THT]
  C1 = Ceramic Capacitor [capacitance=10nF package="100 mil [THT, multilayer]"]
  R2 = Resistor [tolerance=±5% resistance=4.7k package=THT]
  R3 = Resistor [tolerance=±5% resistance=4.7k package=THT]
  C2 = Ceramic Capacitor [capacitance=10nF package="100 mil [THT, multilayer]"]
  C3 = Ceramic Capacitor [capacitance=100nF package="100 mil [THT, multilayer]"]
  R4 = Resistor [tolerance=±5% resistance=10k package=THT]
  J1 = Piezo Speaker
  IC2 = PIC16F690 [package="DIP (Dual Inline) [THT]"]
  J2 = PIC ICSP - 5 pins [form="♂ (male)" package=THT]
  R10 = Resistor [tolerance=±5% resistance=10k package=THT]
  XTAL2 = Crystal [frequency="16 Mhz" package=THT]
  S2 = Pushbutton [package=THT]
  R11 = Resistor [tolerance=±5% resistance=5.2k package=THT]
  R12 = Resistor [tolerance=±5% resistance=10k package=THT]
  R13 = Resistor [tolerance=±5% resistance=220 package=THT]
  U4 = mystery part, 3 pins [chip_label=LM335]
  U5 = mystery part, 3 pins [chip_label=TLE2426]
  R14 = Trimmer Potentiometer [maximum_resistance=100kΩ package=THT]
  D3 = Rectifier Diode [part_number=1N4001 package="300 mil [THT]"]
  D4 = Rectifier Diode [part_number=1N4001 package="300 mil [THT]"]
  R15 = Resistor [tolerance=±5% resistance=27 package=THT]
  R16 = Resistor [tolerance=±5% resistance=1k package=THT]
  U6 = OP37 - Low Noise, Precision, High Speed Op Amp [part_number=OP37]
  R17 = Resistor [tolerance=±5% resistance=1M package=THT]
  R18 = Resistor [tolerance=±5% resistance=1M package=THT]
  LED2 = LED - 5mm [color="Red (633nm)" package="5 mm [THT]"]

nets:
  GND: 512.A0, 512.A1, 512.A2, 512.GND, C1.1, IC2.VSS, J2.pin3, S2.leg1, R13.Pin_0, U4.pin2, U5.pin2, U6.-V, LED2.cathode
  N1: 512.SDA, R1.Pin_1, IC2.RB4
  N2: 512.SCL, IC2.RB6
  VCC: 512.WP, 512.VCC, R1.Pin_0, IC2.VDD, J2.pin2, R10.Pin_0, R11.Pin_0, R12.Pin_0, U5.pin1, U5.pin3, D3.anode, D4.anode, R16.Pin_0, U6.+IN, U6.V+
  N3: C1.0, R2.Pin_0, R3.Pin_0
  N4: R2.Pin_1, IC2.RC5
  N5: R3.Pin_1, C2.1, C3.1
  N6: C2.0, R4.Pin_1, J1.pin2
  N7: C3.0, R4.Pin_0, J1.pin1
  N8: IC2.RA5, XTAL2.pin_0
  N9: IC2.RA4, XTAL2.pin_1
  N10: IC2.RA3, J2.pin1, R10.Pin_1, S2.leg0
  N11: IC2.RC0, LED2.anode
  N12: IC2.RA2, U6.OUT, R17.Pin_0, R18.Pin_0
  N13: IC2.RA1, J2.pin5
  N14: IC2.RA0, J2.pin4
  N15: R11.Pin_1, U4.pin3
  N16: R12.Pin_1, R14.leg2, D4.cathode
  N17: R13.Pin_1, R14.leg1, D3.cathode
  N18: R14.wiper, R15.Pin_0
  N19: R15.Pin_1, R16.Pin_1, U6.-IN, R17.Pin_1, R18.Pin_1

notes:
  Thermocouple
  Pictalker breadboard
  TempertureSensore breadboard

custom parts:
  24LC512: I2C 8x64k flash memory
  PIC16F690: PIC® Flash microcontroller mid-range x14 architecture 2.0-5.5 volts, internal oscillator 8 MHz - 32 KHz, EEPROM, nanoWatt Technology. 12 channels of 10-bit A/D, two comparators, on-chip voltage reference, Enhanced Capture/Compare/PWM, EUSART, SPI/I2C.
  PIC ICSP - 5 pins: PIC ICSP programmer connection (ICP01 PICkit 2 sw)

// code stored in the sketch: test.ino

